// Logisim project ExponentDiff.circ as structural Verilog: 1 circuit, main circuit main
module main (
  input  [8:0] in_1,
  input  [8:0] in_2,
  input  Sa,
  input  Sb,
  output Ea_Eb,
  output [8:0] out_6,
  output [8:0] out_7,
  output Small_Sign,
  output Large_Sign
);

  wire [8:0] multiplexer_3_out;
  wire [9:9] subtractor_1_out;

  Multiplexer multiplexer_1 (.in0(Sa), .in1(Sb), .out(Small_Sign), .sel(Ea_Eb), .en(1'b1));
  Multiplexer multiplexer_2 (.in0(Sb), .in1(Sa), .out(Large_Sign), .sel(Ea_Eb), .en(1'b1));
  Comparator #(.width(9)) comparator_1 (.a(in_1), .b(in_2), .gt(Ea_Eb));  // open: eq, lt
  Multiplexer #(.width(9)) multiplexer_3 (.in0(in_1), .in1(in_2), .out(multiplexer_3_out), .sel(Ea_Eb), .en(1'b1));
  Multiplexer #(.width(9)) multiplexer_4 (.in0(in_2), .in1(in_1), .out(out_7), .sel(Ea_Eb), .en(1'b1));
  Subtractor #(.width(10)) subtractor_1 (
    .a({1'b0, out_7}), .b({1'b0, multiplexer_3_out}), .out({subtractor_1_out[9], out_6}));  // open: bin, bout

  // Notes on the sheet:
  //   Ea
  //   Eb
  //   Large Exponent
  //   Ea~Eb
endmodule
