// Logisim project SEF.circ as structural Verilog: 1 circuit, main circuit main
module main (
  input  [31:0] in_1,
  output [31:0] out_2,
  output [8:0] out_3,
  output Sign
);

  _22to32_main main_1 (.in_1(in_1[21:0]), .out_2(out_2));

  assign out_3 = in_1[30:22];
  assign Sign = in_1[31];

  // Notes on the sheet:
  //   A
  //   Significand
  //   exponent
endmodule
